# Fritzing sketch rover1 (saved by Fritzing 0.9.2b)
breadboards: 1

parts:
  S1 = H-Bridge with L298N
  MLV = DC Motor
  MLA = DC Motor
  MRV = DC Motor
  MRA = DC Motor
  VCC1 = Battery block 9V
  ASV = SRF05 Ultrasonic Rangefinder
  ASA = SRF05 Ultrasonic Rangefinder
  Raspberry_Pi1 = Raspberry Pi 2
  R2V = Resistor [tolerance=±5% resistance=1k package=THT]  # not connected
  R2A = Resistor [tolerance=±5% resistance=1k package=THT]
  R1V = Resistor [tolerance=±5% resistance=550 package=THT]
  R1A = Resistor [tolerance=±5% resistance=550 package=THT]

nets:
  N1: S1.12V, VCC1.+
  GND: S1.GND, VCC1.-, ASV.GND, ASA.GND, Raspberry_Pi1.GND, R2A.Pin_0
  N2: S1.ENA, Raspberry_Pi1.GPIO24
  N3: S1.IN1, Raspberry_Pi1.GPIO17
  N4: S1.IN2, Raspberry_Pi1.GPIO18
  N5: S1.IN3, Raspberry_Pi1.GPIO22
  N6: S1.IN4, Raspberry_Pi1.GPIO23
  N7: S1.ENB, Raspberry_Pi1.GPIO25
  N8: S1.M1-01, MRV.pin_2, MRA.pin_2
  N9: S1.M1-02, MRV.pin_1, MRA.pin_1
  N10: S1.M2-01, MLV.pin_2, MLA.pin_2
  N11: S1.M2-02, MLV.pin_1, MLA.pin_1
  VCC: ASV.VCC, ASA.VCC, Raspberry_Pi1.5V
  N12: ASV.Trig, Raspberry_Pi1.GPIO27
  N13: ASV.Echo, R1V.Pin_1
  N14: ASA.Trig, Raspberry_Pi1.GPIO20
  N15: ASA.Echo, R1A.Pin_1
  N16: Raspberry_Pi1.GPIO4, R1V.Pin_0
  N17: Raspberry_Pi1.GPIO21, R2A.Pin_1, R1A.Pin_0

custom parts:
  H-Bridge with L298N: h-bridge
